# Fritzing sketch Height Measurement Circuit Diagram (saved by Fritzing 1.0.4)
breadboards: 1

parts:
  Part1 = Arduino Nano (Rev3.0) (ICSP)
  HC-SR04_Sensor_1 = HC-SR04 Ultrasonic Distance Sensor
  U1 = LCD-16X2 [package=lcd-16x2_noholes]
  R1 = Rotary Potentiometer (Small) [maximum_resistance=10kΩ knob_status=50% power=0.5W package=THT]

nets:
  GND: Part1.GND, HC-SR04_Sensor_1.GND, U1.VSS, U1.R_W, U1.K, R1.leg1
  N1: Part1.D2, U1.RS
  N2: Part1.D3, U1.E
  N3: Part1.D4, U1.DB4
  N4: Part1.D5, U1.DB5
  N5: Part1.D6, U1.DB6
  N6: Part1.D7, U1.DB7
  N7: Part1.D9, HC-SR04_Sensor_1.ECHO
  N8: Part1.D10, HC-SR04_Sensor_1.TRIG
  5V: Part1.5V, HC-SR04_Sensor_1.VCC, U1.VDD, R1.leg2
  N9: Part1.3V3, U1.A
  N10: U1.VO, R1.wiper
